# Fritzing sketch tally-schematics-ws2812-rgb (saved by Fritzing 0.9.2b)
breadboards: 1

parts:
  U1 = NodeMCU V3.0
  NEOPIXEL1 = Neopixel Strip -- Black (60/m)
  RGB_Strip_LED1 = RGB Strip LED

nets:
  N1: U1.D1, RGB_Strip_LED1.Blue_Connect
  N2: U1.D2, RGB_Strip_LED1.Red_Connect
  N3: U1.D3, RGB_Strip_LED1.Green_Connect
  N4: U1.D4, NEOPIXEL1.DI
  N5: U1.3V3, RGB_Strip_LED1.Common_Connect
  N6: U1.GND#6, U1.GND#13, U1.GND#16, U1.GND#33, NEOPIXEL1.GND
  VIN: U1.Vin, NEOPIXEL1.+5V

notes:
  Stage Lights
  Operator Light

custom parts:
  NodeMCU V3.0: ESP8266 based NodeMCU
  Neopixel Strip -- Black (60/m): Neopixel Strip, Black, 60 pixels per meter.
  RGB Strip LED: A tri-color Strip LED with red, green and blue. Based on LED SMD 5050 RGB Pin order: common cathode - green - red - blue
