# Fritzing sketch tally-schematics-ws2812 (saved by Fritzing 0.9.2b)
breadboards: 1

parts:
  U1 = NodeMCU V3.0
  NEOPIXEL1 = Neopixel Strip -- Black (60/m)
  NEOPIXEL2 = Neopixel Strip -- Black (60/m)

nets:
  N1: U1.D4, NEOPIXEL1.DI
  N2: U1.GND#6, U1.GND#13, U1.GND#16, U1.GND#33, NEOPIXEL1.GND#3
  N3: U1.Vin, NEOPIXEL1.+5V#1
  N4: NEOPIXEL1.GND#4, NEOPIXEL2.GND
  N5: NEOPIXEL1.DO, NEOPIXEL2.DI
  N6: NEOPIXEL1.+5V#6, NEOPIXEL2.+5V

notes:
  Stage Lights
  Operator Light

custom parts:
  NodeMCU V3.0: ESP8266 based NodeMCU
  Neopixel Strip -- Black (60/m): Neopixel Strip, Black, 60 pixels per meter.
