# Fritzing sketch tally-schematics (saved by Fritzing 0.9.2b)
breadboards: 1

parts:
  U1 = NodeMCU V3.0
  RGB_Strip_LED5 = RGB Strip LED
  RGB_Strip_LED6 = RGB Strip LED
  RGB_Strip_LED7 = RGB Strip LED  # not connected
  RGB_Strip_LED8 = RGB Strip LED  # not connected

nets:
  N1: U1.D2, RGB_Strip_LED5.Blue_Connect
  N2: U1.D3, RGB_Strip_LED5.Red_Connect
  N3: U1.D4, RGB_Strip_LED5.Green_Connect
  N4: U1.3V3, RGB_Strip_LED5.Common_Connect, RGB_Strip_LED6.Common_Connect
  N5: U1.GND#6, U1.GND#13, U1.GND#16, U1.GND#33
  N6: U1.D5, RGB_Strip_LED6.Blue_Connect
  N7: U1.D6, RGB_Strip_LED6.Red_Connect
  N8: U1.D7, RGB_Strip_LED6.Green_Connect

notes:
  Stage Lights
  Operator Light

custom parts:
  NodeMCU V3.0: ESP8266 based NodeMCU
  RGB Strip LED: A tri-color Strip LED with red, green and blue. Based on LED SMD 5050 RGB Pin order: common cathode - green - red - blue
